# Fritzing sketch auto-key (saved by Fritzing 0.9.2b)

parts:
  Digispark1 = Digispark
  ENCODER1 = Rotary Encoder with Knob

nets:
  N1: Digispark1.VCC, ENCODER1.no_name_yet#5
  N2: Digispark1.GND, ENCODER1.no_name_yet#2
  N3: Digispark1.P0, ENCODER1.no_name_yet#1
  N4: Digispark1.P1, ENCODER1.no_name_yet#4
  N5: Digispark1.P2, ENCODER1.no_name_yet#3

custom parts:
  Digispark: The Digispark is an Attiny85 based microcontroller development board similar to the Arduino line, only cheaper, smaller, and a bit less powerful. With a whole host of shields to extend its functionality and the ability to use the familiar Arduino IDE the Digispark is a great way to jump into electronics, or perfect for when an Arduino is too big or too much.
  Rotary Encoder with Knob: Rotary Encoder with 1/4" Shaft and Knob
